# Fritzing sketch board (saved by Fritzing 0.9.3b)
breadboards: 1

parts:
  Part1 = Arduino Nano (Rev3.0)
  hc-sr1 = hc-sr04

nets:
  GND: Part1.GND, hc-sr1.GND
  N1: Part1.D6, hc-sr1.Trig
  N2: Part1.D7, hc-sr1.Echo
  5V: Part1.5V, hc-sr1.VCC
